# Fritzing sketch CP 4 Input Circut (saved by Fritzing 0.9.3b)
breadboards: 1

parts:
  Part1 = Arduino Nano (Rev3.0)
  LED1 = LED - 5mm [color="Red (633nm)" package="5 mm [THT]"]
  S1 = Pushbutton [package="[THT]"]
  R1 = Rotary Potentiometer (Small) [maximum_resistance=100kΩ package=THT]
  R2 = Photocell (LDR) [package=THT]
  R3 = Resistor [tolerance=±5% resistance=220 package=THT]

nets:
  N1: Part1.GND, LED1.cathode, S1.Pin_1, S1.Pin_2, S1.Pin_3, S1.Pin_4, R1.leg1, R3.Pin_0
  N2: Part1.5V, Part1.A1, R1.wiper, R2.pin_1, R3.Pin_1
  N3: Part1.A0, R1.leg2
  N4: Part1.D13/SCK, LED1.anode
